# Fritzing sketch Circuito_Nano_Disegno (saved by Fritzing 0.9.2b)
breadboards: 1

parts:
  Componente1 = Arduino Nano (Rev3.0)
  Componente2 = SRF05 Ultrasonic Rangefinder
  U1 = LCD-16X2 [package=lcd-16x2]
  LED2 = smd LED [color="Red (633nm)" package="0805 [SMD]"]
  R2 = Resistor [tolerance=±5% resistance=220 package="0402 [SMD]"]
  LED1 = smd LED [color="Green (555nm)" package="0805 [SMD]"]
  R1 = Resistor [tolerance=±5% resistance=220 package="0402 [SMD]"]
  R3 = Resistor [tolerance=±5% resistance=220 package="0402 [SMD]"]
  VCC1 = Battery block 9V
  U2 = SWITCH-SPST-2 [package=switch-spst-vertical]
  S1 = Momentary Switch [package=ksa_sealed_tac_switch]
  S2 = Momentary Switch [package=ksa_sealed_tac_switch]
  U3 = POT [package=pot_mammoth]
  U4 = SWITCH-SPST-2 [package=switch-spst-vertical]
  LED3 = smd LED [color="Red (633nm)" package="1206 [SMD]"]
  LED4 = smd LED [color="Red (633nm)" package="1206 [SMD]"]
  R4 = Resistor [tolerance=±5% resistance=220 package="0402 [SMD]"]
  R5 = Resistor [tolerance=±5% resistance=220 package="0402 [SMD]"]
  C1 = Electrolytic Capacitor [capacitance=100µF package="200 mil [THT, electrolytic]"]  # not connected
  J1 = Piezo Speaker

nets:
  GND: Componente1.GND, Componente2.GND, U1.VSS, U1.E, U1.K, R2.Pin_0, R1.Pin_0, VCC1.-, U3.S, LED4.cathode, R4.Pin_0, R5.Pin_0, J1.pin1
  N1: Componente1.D2, LED1.anode
  N2: Componente1.D3, U1.VO
  N3: Componente1.D4, LED2.anode
  N4: Componente1.D5, U1.RS
  N5: Componente1.D6, U1.R_W
  N6: Componente1.D7, U1.DB0
  N7: Componente1.D8, U1.DB1
  N8: Componente1.D9, Componente2.Trig
  N9: Componente1.D10, U1.DB2
  N10: Componente1.D11/MOSI, U1.DB3
  N11: Componente1.D12/MISO, U1.DB4
  N12: Componente1.VIN, U2.O
  5V: Componente1.5V, Componente2.VCC, U1.VDD, R3.Pin_0, S1.1, S2.1, U3.E, U4.P
  N13: Componente1.A5, J1.pin2
  N14: Componente1.A4, S1.4, R5.Pin_1
  N15: Componente1.A3, S2.4, R4.Pin_1
  N16: Componente1.A2, Componente2.Echo
  N17: Componente1.A0, U3.A
  N18: U1.A, R3.Pin_1
  N19: LED2.cathode, R2.Pin_1
  N20: LED1.cathode, R1.Pin_1
  N21: VCC1.+, U2.P
  N22: U4.O, LED3.anode
  N23: LED3.cathode, LED4.anode
